// Logisim project TinyCPU_Peripherals.circ as structural Verilog: 4 circuits, main circuit TinyCPUSystemMain
module TinyCPUSystemMain (
  input  CLK,
  input  RESET,
  input  INTERRUPT_REQUEST,
  output [15:0] OUTPUT_PORT_VALUE,
  output OUTPUT_PORT_VALID,
  output INTERRUPT_ENABLED,
  output INTERRUPT_PENDING,
  output IN_INTERRUPT_HANDLER,
  output [11:0] RETURN_ADDRESS,
  output RETURN_ADDRESS_VALID
);
endmodule

module OutputPort (
  input  [15:0] WRITE_VALUE,
  input  WRITE_VALID,
  input  WRITE_ENABLE,
  input  CLK,
  input  RESET,
  output [15:0] VALUE,
  output VALID
);

  Register #(.width(16)) OUTPUT_VALUE (.D(WRITE_VALUE), .en(WRITE_ENABLE), .clk(CLK), .Q(VALUE), .clr(RESET));
  Register #(.width(1)) OUTPUT_VALID (.D(WRITE_VALID), .en(WRITE_ENABLE), .clk(CLK), .Q(VALID), .clr(RESET));
endmodule

module OutputMemoryPath (
  input  [15:0] RAM_READ_VALUE,
  input  RAM_READ_VALID,
  input  [11:0] ADDRESS,
  input  [15:0] WRITE_VALUE,
  input  WRITE_ENABLE,
  input  WRITE_VALID,
  input  CLK,
  input  RESET,
  output [15:0] READ_VALUE,
  output READ_VALID,
  output [15:0] OUTPUT_PORT_VALUE,
  output OUTPUT_PORT_VALID,
  output RAM_WRITE_ENABLE
);

  wire comparator_1_eq, PORT_WRITE_out;

  Comparator #(.width(12)) comparator_1 (.a(ADDRESS), .b({12{1'b1}}), .eq(comparator_1_eq));  // open: gt, lt
  and PORT_WRITE (PORT_WRITE_out, comparator_1_eq, WRITE_ENABLE);
  and RAM_WRITE (RAM_WRITE_ENABLE, ~comparator_1_eq, WRITE_ENABLE);  // AND_Gate
  Register #(.width(16)) OUTPUT_VALUE (
    .D(WRITE_VALUE), .en(PORT_WRITE_out), .clk(CLK), .Q(OUTPUT_PORT_VALUE), .clr(RESET));
  Register #(.width(1)) OUTPUT_VALID (
    .D(WRITE_VALID), .en(PORT_WRITE_out), .clk(CLK), .Q(OUTPUT_PORT_VALID), .clr(RESET));
  Multiplexer #(.width(16)) multiplexer_1 (
    .in0(RAM_READ_VALUE), .in1(OUTPUT_PORT_VALUE), .out(READ_VALUE), .sel(comparator_1_eq));
  Multiplexer multiplexer_2 (.in0(RAM_READ_VALID), .in1(OUTPUT_PORT_VALID), .out(READ_VALID), .sel(comparator_1_eq));

  // Notes on the sheet:
  //   OUTPUT MEMORY PATH — address 0xFFF selects output port
endmodule

module InterruptController (
  input  INTERRUPT_REQUEST,
  input  INSTRUCTION_BOUNDARY,
  input  ENABLE_REQUEST,
  input  DISABLE_REQUEST,
  input  [11:0] NEXT_PC,
  input  RETURN_REQUEST,
  input  CLK,
  input  RESET,
  output INTERRUPT_ACCEPT,
  output INTERRUPT_PENDING,
  output INTERRUPT_ENABLED,
  output [11:0] RETURN_ADDRESS,
  output [11:0] TARGET_PC,
  output ILLEGAL_RETURN,
  output RETURN_ADDRESS_VALID,
  output IN_INTERRUPT_HANDLER
);

  wire HANDLER_HOLD_out, HANDLER_NEXT_out, MASK_HOLD_out, MASK_NEXT_out, PENDING_HOLD_out, PENDING_NEXT_out,
       REQUEST_LEVEL_q, RETURN_VALID_HOLD_out, RETURN_VALID_NEXT_out, RISING_EDGE_out, VALID_RETURN_out;

  and RISING_EDGE (RISING_EDGE_out, ~REQUEST_LEVEL_q, INTERRUPT_REQUEST);  // AND_Gate
  and PENDING_HOLD (PENDING_HOLD_out, INTERRUPT_PENDING, ~INTERRUPT_ACCEPT);  // AND_Gate
  and MASK_HOLD (MASK_HOLD_out, INTERRUPT_ENABLED, ~DISABLE_REQUEST, ~INTERRUPT_ACCEPT);  // AND_Gate
  and RETURN_VALID_HOLD (RETURN_VALID_HOLD_out, RETURN_ADDRESS_VALID, ~VALID_RETURN_out);  // AND_Gate
  and HANDLER_HOLD (HANDLER_HOLD_out, IN_INTERRUPT_HANDLER, ~VALID_RETURN_out);  // AND_Gate
  or PENDING_NEXT (PENDING_NEXT_out, RISING_EDGE_out, PENDING_HOLD_out);
  or MASK_NEXT (MASK_NEXT_out, ENABLE_REQUEST, VALID_RETURN_out, MASK_HOLD_out);
  or RETURN_VALID_NEXT (RETURN_VALID_NEXT_out, INTERRUPT_ACCEPT, RETURN_VALID_HOLD_out);
  or HANDLER_NEXT (HANDLER_NEXT_out, INTERRUPT_ACCEPT, HANDLER_HOLD_out);
  Register #(.width(1)) REQUEST_LEVEL (.D(INTERRUPT_REQUEST), .en(1'b1), .clk(CLK), .Q(REQUEST_LEVEL_q), .clr(RESET));
  Register #(.width(1)) register_1 (.D(PENDING_NEXT_out), .en(1'b1), .clk(CLK), .Q(INTERRUPT_PENDING), .clr(RESET));
  Register #(.width(1)) register_2 (.D(MASK_NEXT_out), .en(1'b1), .clk(CLK), .Q(INTERRUPT_ENABLED), .clr(RESET));
  Register #(.width(12)) register_3 (.D(NEXT_PC), .en(INTERRUPT_ACCEPT), .clk(CLK), .Q(RETURN_ADDRESS), .clr(RESET));
  Register #(.width(1)) register_4 (
    .D(RETURN_VALID_NEXT_out), .en(1'b1), .clk(CLK), .Q(RETURN_ADDRESS_VALID), .clr(RESET));
  Register #(.width(1)) register_5 (.D(HANDLER_NEXT_out), .en(1'b1), .clk(CLK), .Q(IN_INTERRUPT_HANDLER), .clr(RESET));
  and ACCEPT (INTERRUPT_ACCEPT, INSTRUCTION_BOUNDARY, INTERRUPT_PENDING, INTERRUPT_ENABLED, ~IN_INTERRUPT_HANDLER);  // AND_Gate
  and VALID_RETURN (VALID_RETURN_out, RETURN_REQUEST, IN_INTERRUPT_HANDLER, RETURN_ADDRESS_VALID);
  Multiplexer #(.width(12)) multiplexer_1 (
    .in0(12'hff0), .in1(RETURN_ADDRESS), .out(TARGET_PC), .sel(VALID_RETURN_out));
  and and_1 (ILLEGAL_RETURN, RETURN_REQUEST, ~VALID_RETURN_out);  // AND_Gate

  // Notes on the sheet:
  //   EDGE / INPUTS
  //   NEXT-STATE LOGIC
  //   feedback buses: ACCEPT / VALID_RETURN
  //   STATE REGISTERS
  //   ACCEPT / RETURN DECODE
endmodule
